# Fritzing sketch WiringDiagram (saved by Fritzing 0.9.5d)
stripboards: 1

parts:
  M4 = Stepper Motor - Bipolar
  M5 = Stepper Motor - Bipolar
  HC-SR04_Sensor_1 = HC-SR04 Ultrasonic Distance Sensor
  Mod1 = ESP32 - CAM
  Mod2 = ESP32 - CAM
  M6 = RioRand LM2596
  BMS1 = BMS
  ESP1 = DIP - 42 pins
  LiPo1 = DIP - 6 pins [package=Battery]
  IC1 = DIP - 8 pins [chip_label=IC package="DIP (Dual Inline) [THT]"]
  IC2 = DIP - 8 pins [chip_label=IC package="DIP (Dual Inline) [THT]"]
  L298N1 = L298N DC motor driver
  Arduino_CNC_Shield_V3_00_1 = Arduino_CNC_V3.00
  SM1 = 28BYJ-48 Stepper Motor [part_number=28BYJ-48]
  SM2 = 28BYJ-48 Stepper Motor [part_number=28BYJ-48]
  Driver1 = 28BYJ-48 Driver Module [part_number=ULN2003 package=THT]
  Driver2 = 28BYJ-48 Driver Module [part_number=ULN2003 package=THT]

nets:
  N1: M4.A, Arduino_CNC_Shield_V3_00_1.X-MTR_'1'
  N2: M4.C, Arduino_CNC_Shield_V3_00_1.X-MTR_'2'
  N3: M4.B, Arduino_CNC_Shield_V3_00_1.X-MTR_'3'
  N4: M4.D, Arduino_CNC_Shield_V3_00_1.X-MTR_'4'
  N5: M5.A, Arduino_CNC_Shield_V3_00_1.Y-MTR_'1'
  N6: M5.C, Arduino_CNC_Shield_V3_00_1.Y-MTR_'2'
  N7: M5.B, Arduino_CNC_Shield_V3_00_1.Y-MTR_'3'
  N8: M5.D, Arduino_CNC_Shield_V3_00_1.Y-MTR_'4'
  5V: HC-SR04_Sensor_1.VCC, Mod1.5V, Mod2.5V, M6.Pin_3, ESP1.5v0, Arduino_CNC_Shield_V3_00_1.5V, Driver1.Vmotor, Driver2.Vmotor
  N9: HC-SR04_Sensor_1.TRIG, ESP1.GPIO13
  N10: HC-SR04_Sensor_1.ECHO, ESP1.GPIO12
  GND: HC-SR04_Sensor_1.GND, Mod1.GND, Mod2.GND, M6.Pin_4, ESP1.GND, Arduino_CNC_Shield_V3_00_1.EN(able), Arduino_CNC_Shield_V3_00_1.GND, Driver1.GND, Driver2.GND
  N11: M6.Pin_1, BMS1.Load_+, L298N1.12V, Arduino_CNC_Shield_V3_00_1.POWER_+
  N12: M6.Pin_2, BMS1.Load_-, L298N1.GND, Arduino_CNC_Shield_V3_00_1.POWER_-
  N13: BMS1.0V, LiPo1.V-, LiPo1.0V
  N14: BMS1.4.2V, LiPo1.4.2V
  N15: BMS1.8.4V, LiPo1.8.4V
  N16: BMS1.12.6V, LiPo1.V+, LiPo1.12.6V
  N17: ESP1.GPIO01, L298N1.ENB
  N18: ESP1.GPIO02, L298N1.IN4
  N19: ESP1.GPIO03, L298N1.IN3
  N20: ESP1.GPIO04, L298N1.IN2
  N21: ESP1.GPIO05, L298N1.IN1
  N22: ESP1.GPIO06, L298N1.ENA
  N23: ESP1.GPIO07, Arduino_CNC_Shield_V3_00_1.Y.DIR
  N24: ESP1.GPIO08, Arduino_CNC_Shield_V3_00_1.Y.STEP
  N25: ESP1.GPIO09, Arduino_CNC_Shield_V3_00_1.X.DIR
  N26: ESP1.GPIO10, Arduino_CNC_Shield_V3_00_1.X.STEP
  N27: ESP1.GPIO35, Driver2.IN1
  N28: ESP1.GPIO34, Driver2.IN2
  N29: ESP1.GPIO33, Driver2.IN3
  N30: ESP1.GPIO26, Driver2.IN4
  N31: ESP1.GPIO21, Driver1.IN1
  N32: ESP1.GPIO20, Driver1.IN2
  N33: ESP1.GPIO19, Driver1.IN3
  N34: ESP1.GPIO18, Driver1.IN4
  N35: IC1.red, L298N1.OUT2
  N36: IC1.black, IC1.blue, L298N1.OUT1
  N37: IC2.red, L298N1.OUT3
  N38: IC2.black, L298N1.OUT4
  N39: SM1.blue-pin, Driver1.blue-pin
  N40: SM1.pink-pin, Driver1.pink-pin
  N41: SM1.yellow-pin, Driver1.yellow-pin
  N42: SM1.orange-pin, Driver1.orange-pin
  N43: SM1.red-pin, Driver1.red-pin
  N44: SM2.blue-pin, Driver2.blue-pin
  N45: SM2.pink-pin, Driver2.pink-pin
  N46: SM2.yellow-pin, Driver2.yellow-pin
  N47: SM2.orange-pin, Driver2.orange-pin
  N48: SM2.red-pin, Driver2.red-pin

custom parts:
  ESP32 - CAM: The ESP32-CAM has a very competitive small-size camera module that can operate independently as a minimum system with a footprint of only 27*40.5*4.5mm and a deep sleep current of up to 6mA.
  BMS: BMS for 3S battery
  DIP - 42 pins: ESP32-S2-DevKitM-1
  DIP - 6 pins: A LiPo 3S
  DIP - 8 pins: A DIP stand-in part for whatever IC you want. With 8 pins on a 300mil dual inline package (DIP) footprint.
  L298N DC motor driver: 2x DC motor driver with 78M05 positive voltage regulator (7..35 V) L298N: max 46 V, 2 A Set 5 V Enable jumper to enable 5 V regultor (needed for the L298N) and +5 V output at screw terminal or supply external +5 V at screw terminal Set ENA and/or ENB to +5 V to enable motor permanently or supply ENA and/or ENB with PWM signal IN1 and IN2 set rotation directory for motor A (OUT1/OUT2) IN2 and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
  Arduino_CNC_V3.00: Protoneer Arduino CNC Shield V3.00 If using Grbl V0.9: The “A” axis can not be used (yet). The “SCL” (Arduino A5) pin is now used for 'Probing' input. The “End Stops Z+ & Z-” (Arduino D11) and “SpnEn” (Arduino D12) have been switched!
  28BYJ-48 Stepper Motor: Unipolar Stepper Motor 28BYJ-48 Top coil - pink & orange Bottom coil - blue & yellow Common rail - red Connector pins: blue - pink - yellow - orange - red
  28BYJ-48 Driver Module: ULN2003 Driver Module for the 28BYJ-48 Unipolar Stepper Motor LED A - Blue wire - Bottom coil left LED B - Pink wire - Top coil left LED C - Yellow wire - Bottom coil right LED D - Orange wire - Top coil right Common rail - red Connector pins: blue - pink - yellow - orange - red Control pins - IN1 to IN4 Power pins - GND & Vmotor (5-12V) On/Off jumper (if removed, power to motor is cut).
